# Fritzing sketch joystick-matrix (saved by Fritzing 1.0.4)
breadboards: 1

parts:
  Disp1 = 20mm 8x8 dot matrix row cathode led display with standard pcb pads
  Part1 = Arduino Uno (Rev3) - ICSP
  Part2 = Thumb Joystick

nets:
  N1: Disp1.pin_1, Part1.D13/SCK
  N2: Disp1.pin_2, Part1.D12/MISO
  N3: Disp1.pin_3, Part1.D11_PWM/MOSI
  N4: Disp1.pin_4, Part1.D10_PWM/SS
  N5: Disp1.pin_5, Part1.A2
  N6: Disp1.pin_6, Part1.A3
  N7: Disp1.pin_7, Part1.A4/SDA
  N8: Disp1.pin_8, Part1.A5/SCL
  N9: Disp1.pin_9, Part1.D2
  N10: Disp1.pin_10, Part1.D3_PWM
  N11: Disp1.pin_11, Part1.D4
  N12: Disp1.pin_12, Part1.D5_PWM
  N13: Disp1.pin_13, Part1.D6_PWM
  N14: Disp1.pin_14, Part1.D7
  N15: Disp1.pin_15, Part1.D8
  N16: Disp1.pin_16, Part1.D9_PWM
  N17: Part1.A0, Part2.HORZ
  N18: Part1.A1, Part2.VERT
  5V: Part1.5V, Part2.VCC
  GND: Part1.GND, Part2.GND
